# Fritzing sketch phase3 (saved by Fritzing 0.9.3b)
breadboards: 1

parts:
  Part1 = SparkFun ESP8266 Thing  # not connected
  LED1 = LED - 5mm [color="Red (633nm)" package="5 mm [THT]"]
  R1 = Resistor [tolerance=±5% resistance=220 package=THT]
  Raspberry_Pi_1 = Raspberry Pi 3 [part_number=RPI-3-V1.2]
  R2 = Photocell (LDR) [package=THT]
  R3 = Resistor [tolerance=±5% resistance=10k package=THT]

nets:
  N1: LED1.cathode, R1.Pin_0
  N2: LED1.anode, Raspberry_Pi_1.GIPO4
  N3: R1.Pin_1, Raspberry_Pi_1.GND, R3.Pin_1
  N4: Raspberry_Pi_1.GIPO18, R2.pin_0
  N5: R2.pin_1, R3.Pin_0
